# Fritzing sketch Pi Zero Sketch (saved by Fritzing 0.9.3b)
breadboards: 1

parts:
  Raspberry_Pi_Zero1 = Raspberry Pi Zero
  Part1 = LED Tactile Button Breakout v10 [part_number=BOB-10467]

nets:
  N1: Raspberry_Pi_Zero1.GPIO2, Part1.3
  N2: Raspberry_Pi_Zero1.GND, Part1.1, Part1.4
  N3: Raspberry_Pi_Zero1.GPIO17, Part1.2
